# Fritzing sketch Remote (saved by Fritzing 0.9.3b)
breadboards: 1

parts:
  Nano1 = Arduino Nano v2.3
  MPU9250_MPU-1 = SparkFun IMU Breakout - MPU-9250 [part_number=" SEN-13762"]
  S1 = Pushbutton [package="[SMD]"]
  R1 = Resistor [tolerance=±5% resistance=10 package="1206 [SMD]"]

nets:
  N1: Nano1.D7, S1.Pin_1, S1.Pin_2
  N2: Nano1.A5, MPU9250_MPU-1.SCL/SCLK
  N3: Nano1.A4, MPU9250_MPU-1.SDA/SDI
  +5V: Nano1.+5V, MPU9250_MPU-1.VDD
  GND: Nano1.GND, MPU9250_MPU-1.GND, R1.Pin_1
  N4: S1.Pin_3, S1.Pin_4, R1.Pin_0
